// Logisim project 4_bit_adder.circ as structural Verilog: 1 circuit, main circuit main
module main (
  input  Cin,
  input  A0,
  input  B0,
  input  A1,
  input  B1,
  input  A2,
  input  B2,
  input  A3,
  input  B3
);

  wire and_1_out, and_2_out, and_3_out, and_4_out, and_5_out, and_6_out, and_7_out, and_8_out, and_9_out,
       and_10_out, and_11_out, and_12_out, or_1_out, or_2_out, or_3_out, or_4_out, xor_1_out, xor_2_out,
       xor_3_out, xor_4_out;

  ExactlyOne xor_1 (.out(xor_1_out), .in0(Cin), .in1(A0), .in2(B0));
  ExactlyOne xor_2 (.out(xor_2_out), .in0(A1), .in1(B1), .in2(or_1_out));
  ExactlyOne xor_3 (.out(xor_3_out), .in0(A2), .in1(B2), .in2(or_2_out));
  ExactlyOne xor_4 (.out(xor_4_out), .in0(A3), .in1(B3), .in2(or_3_out));
  and and_1 (and_1_out, A0, B0);
  and and_2 (and_2_out, B0, Cin);
  and and_3 (and_3_out, A0, Cin);
  and and_4 (and_4_out, A1, B1);
  and and_5 (and_5_out, A1, or_1_out);
  and and_6 (and_6_out, B1, or_1_out);
  and and_7 (and_7_out, A2, B2);
  and and_8 (and_8_out, A2, or_2_out);
  and and_9 (and_9_out, B2, or_2_out);
  and and_10 (and_10_out, A3, B3);
  and and_11 (and_11_out, A3, or_3_out);
  and and_12 (and_12_out, B3, or_3_out);
  LED S0 (.in(xor_1_out));
  or or_1 (or_1_out, and_1_out, and_2_out, and_3_out);
  LED S1 (.in(xor_2_out));
  or or_2 (or_2_out, and_4_out, and_5_out, and_6_out);
  LED S2 (.in(xor_3_out));
  or or_3 (or_3_out, and_7_out, and_8_out, and_9_out);
  LED S3 (.in(xor_4_out));
  or or_4 (or_4_out, and_10_out, and_11_out, and_12_out);
  LED Cout (.in(or_4_out));
endmodule
